// Logisim project binary_search_tree.circ as structural Verilog: 2 circuits, main circuit main
module main (
  input  [4:0] poszukiwany,
  output brak,
  output [4:0] aktualnie_sprawdzany_numer,
  output czy_znaleziono,
  output [3:0] lokalizacja,
  output [3:0] aktualnie_sprawdzany_adres
);

  wire and_3_out, clock_1_out, comparator_1_eq, comparator_1_gt;
  wire [3:0] adder_1_out, adder_2_out, and_1_out, and_2_out, register_1_q, register_2_q, subtractor_1_out;
  wire [3:3] comparator_2_gt, comparator_2_lt;
  wire [4:4] adder_2_cout, shifter_1_out;

  Clock clock_1 (.out(clock_1_out));
  Register #(.width(4)) register_1 (
    .D(and_1_out), .en(comparator_2_lt[3]), .clk(clock_1_out), .Q(register_1_q));  // open: clr
  assign and_1_out = adder_1_out & {4{comparator_2_lt[3]}};  // AND_Gate and_1, 4 bits wide
  Register #(.width(4)) register_2 (
    .D(and_2_out), .en(comparator_2_gt[3]), .clk(clock_1_out), .Q(register_2_q));  // open: clr
  Adder #(.width(4)) adder_1 (.a(aktualnie_sprawdzany_adres), .b(4'b0001), .out(adder_1_out));  // open: cin, cout
  Comparator #(.width(4)) comparator_1 (
    .a(register_1_q), .b(register_2_q), .gt(comparator_1_gt), .eq(comparator_1_eq));  // open: lt
  assign and_2_out = {4{comparator_2_gt[3]}} & subtractor_1_out;  // AND_Gate and_2, 4 bits wide
  Adder #(.width(4)) adder_2 (
    .a(register_1_q), .b(register_2_q), .out(adder_2_out), .cout(adder_2_cout[4]));  // open: cin
  Shifter #(.shift("lr"), .width(5)) shifter_1 (
    .in({adder_2_cout[4], adder_2_out}), .\dist (3'b001), .out({shifter_1_out[4], aktualnie_sprawdzany_adres}));
  buf and_3 (and_3_out, ~czy_znaleziono);  // AND_Gate AND_Gate
  Subtractor #(.width(4)) subtractor_1 (
    .a(aktualnie_sprawdzany_adres), .b(4'b0001), .out(subtractor_1_out));  // open: bin, bout
  memory memory_1 (.in_1(aktualnie_sprawdzany_adres), .out_2(aktualnie_sprawdzany_numer));
  or or_1 (brak, comparator_1_gt, and_3_out);
  Comparator #(.width(5)) comparator_2 (
    .a(aktualnie_sprawdzany_numer), .b(poszukiwany), .gt(comparator_2_gt[3]), .eq(czy_znaleziono),
    .lt(comparator_2_lt[3]));
  assign lokalizacja = {4{czy_znaleziono}} & aktualnie_sprawdzany_adres;  // AND_Gate and_4, 4 bits wide
endmodule

module memory (
  input  [3:0] in_1,
  output [4:0] out_2
);

  Multiplexer #(.select(4), .width(5)) multiplexer_1 (
    .in0({5{1'b0}}), .in1(5'b00001), .in2(5'b00010), .in3(5'b00011), .in4(5'b00100), .in5(5'b00101),
    .in6(5'b00110), .in7(5'b00111), .in8(5'b01000), .in9(5'b01001), .in10(5'b01010), .in11(5'b01011),
    .in12(5'b01100), .in13(5'b01101), .in14(5'b01110), .in15(5'b01111), .out(out_2), .sel(in_1));
endmodule
